# Fritzing sketch ESP32-Devkit-v1-30pin (saved by Fritzing 0.9.4)

parts:
  U1 = ESP32 DEVKIT V1 DOIT [part_number=ESP32S-HiLetgo]
  Part3 = Waveshare 4.2" 400×300 ePaper Display Module
  Part4 = BME280 Breakout

nets:
  N1: U1.3.3, Part3.VCC
  GND: U1.GND, Part3.GND, Part4.GND
  N2: U1.GPIO13, Part4.VCC
  N3: U1.GPIO15, Part3.BUSY
  N4: U1.GPIO2, Part3.RST
  N5: U1.GPIO4, Part3.DC
  N6: U1.GPIO5, Part3.CS
  N7: U1.GPIO18, Part3.CLK
  N8: U1.GPIO21, Part4.SDA
  N9: U1.GPIO22, Part4.SCL
  N10: U1.GPIO23, Part3.DIN

custom parts:
  ESP32 DEVKIT V1 DOIT: 30GPIO Version
  BME280 Breakout: SparkFun Atmospheric Sensor Breakout - BME280 SEN-13676 The SparkFun BME280 Atmospheric Sensor Breakout is the easy way to measure barometric pressure, humidity, and temperature readings all without taking up too much space. Basically, anything you need to know about atmospheric conditions you can find out from this tiny breakout. The BME280 Breakout has been design to be used in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
