# Fritzing sketch Wemos-D1-mini (saved by Fritzing 0.9.4)

parts:
  Part1 = BME280 Breakout
  WeMos_D1_Mini1 = WeMos D1 Mini
  Part2 = Waveshare 4.2" 400×300 ePaper Display Module

nets:
  N1: Part1.VCC, WeMos_D1_Mini1.D4
  GND: Part1.GND, WeMos_D1_Mini1.G, Part2.GND
  N2: Part1.SCL, WeMos_D1_Mini1.D1
  N3: Part1.SDA, WeMos_D1_Mini1.D2
  3V3: WeMos_D1_Mini1.3V3, Part2.VCC
  N4: WeMos_D1_Mini1.D0, Part2.RST
  N5: WeMos_D1_Mini1.D3, Part2.DC
  N6: WeMos_D1_Mini1.D5, Part2.CLK
  N7: WeMos_D1_Mini1.D6, Part2.BUSY
  N8: WeMos_D1_Mini1.D7, Part2.DIN
  N9: WeMos_D1_Mini1.D8, Part2.CS

custom parts:
  BME280 Breakout: SparkFun Atmospheric Sensor Breakout - BME280 SEN-13676 The SparkFun BME280 Atmospheric Sensor Breakout is the easy way to measure barometric pressure, humidity, and temperature readings all without taking up too much space. Basically, anything you need to know about atmospheric conditions you can find out from this tiny breakout. The BME280 Breakout has been design to be used in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
